// Logisim project progetto.circ as structural Verilog: 5 circuits, main circuit main
module main (
  output [4:0] out_1,
  output [4:0] out_2,
  output [4:0] out_3,
  output [4:0] out_4
);

  wire _0_out, _1_out, _2_out, _3_out, _4_out, _5_out, _6_out, _7_out, _8_out, _9_out, button_2_out,
       button_out, keypad_1_clicked, minus_1_out_2, OK_out, or_1_out;
  wire [1:0] counter_1_q;
  wire [3:0] keypad_1_b0;
  wire [4:0] multiplexer_1_out, negativator_1_out_2;

  Button _8 (.out(_8_out));
  Button _7 (.out(_7_out));
  Button _9 (.out(_9_out));
  Button _4 (.out(_4_out));
  Button _5 (.out(_5_out));
  Button _6 (.out(_6_out));
  Button _3 (.out(_3_out));
  Button _2 (.out(_2_out));
  Button _1 (.out(_1_out));
  Button _0 (.out(_0_out));
  Button OK (.out(OK_out));
  Button button (.out(button_out));
  Button button_2 (.out(button_2_out));
  or or_1 (or_1_out, OK_out, button_out);
  keypad keypad_1 (
    ._0(_0_out), ._1(_1_out), ._3(_3_out), ._2(_2_out), ._5(_5_out), ._4(_4_out), ._7(_7_out), ._6(_6_out),
    .b2_2(keypad_1_b0[2]), .b1(keypad_1_b0[1]), .b0(keypad_1_b0[0]), ._8(_8_out), ._9(_9_out),
    .b2(keypad_1_b0[3]), .clicked(keypad_1_clicked));
  minus minus_1 (.in_1(button_2_out), .out_2(minus_1_out_2));
  LED led_1 (.in(minus_1_out_2));
  Counter #(.width(2), .max('h2), .trigger("falling")) counter_1 (
    .Q(counter_1_q), .clk(or_1_out));  // open: load, D, count, carry, clr
  negativator negativator_1 (.in_1({1'b0, keypad_1_b0}), .out_2(negativator_1_out_2));
  Multiplexer #(.width(5)) multiplexer_1 (
    .in0({1'b0, keypad_1_b0}), .in1(negativator_1_out_2), .out(multiplexer_1_out), .sel(minus_1_out_2));  // open: en
  memory memory_1 (
    .in_1(multiplexer_1_out), .in_2(keypad_1_clicked), .in_3(OK_out), .in_4(counter_1_q), .out_5(out_1),
    .out_6(out_2), .out_7(out_3), .out_8(out_4));
endmodule

module keypad (
  input  _0,
  input  _1,
  input  _3,
  input  _2,
  input  _5,
  input  _4,
  input  _7,
  input  _6,
  input  _9,
  input  _8,
  output clicked,
  output b2,
  output b2_2,
  output b1,
  output b0
);

  or or_1 (b0, _1, _9, _3, _5, _7);
  or or_2 (b1, _3, _2, _7, _6);
  or or_3 (b2_2, _6, _5, _7, _4);
  or or_4 (b2, _9, _8);
  or or_5 (clicked, _0, b0, b1, b2_2, b2);
endmodule

module negativator (
  input  [4:0] in_1,
  output [4:0] out_2
);

  wire [4:0] not_1_out;

  assign not_1_out = ~in_1;  // NOT_Gate not_1, 5 bits wide
  Adder #(.width(5)) adder_1 (.a(not_1_out), .b(5'b00001), .out(out_2));  // open: cin, cout
endmodule

module memory (
  input  [4:0] in_1,
  input  in_2,
  input  in_3,
  input  [1:0] in_4,
  output [4:0] out_5,
  output [4:0] out_6,
  output [4:0] out_7,
  output [4:0] out_8
);

  wire demultiplexer_2_out0, demultiplexer_2_out1, demultiplexer_2_out2, demultiplexer_2_out3;
  wire [4:0] d_ff_1_q, demultiplexer_1_out0, demultiplexer_1_out1, demultiplexer_1_out2, demultiplexer_1_out3;

  D_Flip_Flop #(.trigger("high")) d_ff_1 (.clk(in_2), .D(in_1[0]), .Q(d_ff_1_q[0]));  // open: Qn, preset, en, reset
  D_Flip_Flop #(.trigger("high")) d_ff_2 (.clk(in_2), .D(in_1[1]), .Q(d_ff_1_q[1]));  // open: Qn, preset, en, reset
  D_Flip_Flop #(.trigger("high")) d_ff_3 (.clk(in_2), .D(in_1[2]), .Q(d_ff_1_q[2]));  // open: Qn, preset, en, reset
  D_Flip_Flop #(.trigger("high")) d_ff_4 (.clk(in_2), .D(in_1[3]), .Q(d_ff_1_q[3]));  // open: Qn, preset, en, reset
  D_Flip_Flop #(.trigger("high")) d_ff_5 (.clk(in_2), .D(in_1[4]), .Q(d_ff_1_q[4]));  // open: Qn, preset, en, reset
  Demultiplexer #(.select(2), .width(5)) demultiplexer_1 (
    .out0(demultiplexer_1_out0), .out1(demultiplexer_1_out1), .out2(demultiplexer_1_out2),
    .out3(demultiplexer_1_out3), .in(d_ff_1_q), .sel(in_4));  // open: en
  Demultiplexer #(.select(2)) demultiplexer_2 (
    .out0(demultiplexer_2_out0), .out1(demultiplexer_2_out1), .out2(demultiplexer_2_out2),
    .out3(demultiplexer_2_out3), .in(in_3), .sel(in_4));  // open: en
  Register #(.width(5), .trigger("high")) register_1 (
    .D(demultiplexer_1_out0), .Q(out_5), .clk(demultiplexer_2_out0));  // open: en, clr
  Register #(.width(5), .trigger("high")) register_2 (
    .D(demultiplexer_1_out1), .Q(out_6), .clk(demultiplexer_2_out1));  // open: en, clr
  Register #(.width(5), .trigger("high")) register_3 (
    .D(demultiplexer_1_out2), .Q(out_7), .clk(demultiplexer_2_out2));  // open: en, clr
  Register #(.width(5), .trigger("high")) register_4 (
    .D(demultiplexer_1_out3), .Q(out_8), .clk(demultiplexer_2_out3));  // open: en, clr
endmodule

module minus (
  input  in_1,
  output out_2
);

  wire and_1_out, d_ff_1_qn;

  and and_1 (and_1_out, in_1, d_ff_1_qn);
  D_Flip_Flop #(.trigger("falling")) d_ff_1 (
    .clk(in_1), .D(and_1_out), .Q(out_2), .Qn(d_ff_1_qn));  // open: preset, en, reset
endmodule
